# Fritzing sketch Fritzing Sketch Source File (saved by Fritzing 0.9.3b)
breadboards: 1

parts:
  Part3 = Arduino Uno (Rev3)
  U3 = LCD-16X2 [package=lcd-16x2]
  LCM1602_IIC3 = LCM1602 IIC [part_number="LCM1602 IIC" chip_label="LCM1602 IIC" package="DIP (Dual Inline) [THT]"]
  S1 = Round Pushbutton
  S2 = Round Pushbutton
  S3 = Round Pushbutton
  S4 = Round Pushbutton
  S6 = Round Pushbutton
  S7 = Round Pushbutton

nets:
  N1: Part3.A4/SDA, LCM1602_IIC3.SDA
  N2: Part3.A5/SCL, LCM1602_IIC3.SCL
  N3: Part3.D8, S6.leg0
  N4: Part3.D3_PWM, S1.leg0
  N5: Part3.D4, S2.leg0
  N6: Part3.D5_PWM, S3.leg0
  N7: Part3.D6_PWM, S4.leg0
  N8: Part3.D7, S7.leg0
  5V: Part3.5V, LCM1602_IIC3.VCC
  GND: Part3.GND, LCM1602_IIC3.GND, S1.leg1, S2.leg1, S3.leg1, S4.leg1, S6.leg1, S7.leg1
  N9: U3.VSS, LCM1602_IIC3.K
  N10: U3.VDD, LCM1602_IIC3.A
  N11: U3.VO, LCM1602_IIC3.D7
  N12: U3.RS, LCM1602_IIC3.D6
  N13: U3.R_W, LCM1602_IIC3.D5
  N14: U3.E, LCM1602_IIC3.D4
  N15: U3.DB0, LCM1602_IIC3.D3
  N16: U3.DB1, LCM1602_IIC3.D2
  N17: U3.DB2, LCM1602_IIC3.D1
  N18: U3.DB3, LCM1602_IIC3.D0
  N19: U3.DB4, LCM1602_IIC3.E
  N20: U3.DB5, LCM1602_IIC3.RW
  N21: U3.DB6, LCM1602_IIC3.RS
  N22: U3.DB7, LCM1602_IIC3.V0
  N23: U3.A, LCM1602_IIC3.VDD
  N24: U3.K, LCM1602_IIC3.VSS

notes:
  GND - Green
  5VC - Red
  GPIO - Blue
  Developed By Web Dev Fusion
  www.webdevfusion.com

custom parts:
  LCM1602 IIC: I2C-Module to use a 1602 or 2004 LCD on with the wire.h libory Serial LCD Modul
